// Logisim project Assignment.circ as structural Verilog: 12 circuits, main circuit Full Adder
module Full_Adder (
  input  A,
  input  B,
  input  C_in,
  output S,
  output C_out
);

  wire and_1_out, and_2_out, and_3_out, xor_1_out;

  xor xor_1 (xor_1_out, B, C_in);
  and and_1 (and_1_out, A, B);
  and and_2 (and_2_out, A, C_in);
  and and_3 (and_3_out, B, C_in);
  xor xor_2 (S, A, xor_1_out);
  or or_1 (C_out, and_1_out, and_2_out, and_3_out);
endmodule

module Ripple_Carry_Adder (
  input  [3:0] A,
  input  [3:0] B,
  input  in_3,
  output [3:0] Sum,
  output C_out
);

  wire full_adder_1_c_out, full_adder_2_c_out, full_adder_3_c_out;

  Full_Adder full_adder_1 (.A(B[0]), .B(A[0]), .C_in(in_3), .S(Sum[0]), .C_out(full_adder_1_c_out));
  Full_Adder full_adder_2 (.A(B[1]), .B(A[1]), .C_in(full_adder_1_c_out), .S(Sum[1]), .C_out(full_adder_2_c_out));
  Full_Adder full_adder_3 (.A(B[2]), .B(A[2]), .C_in(full_adder_2_c_out), .S(Sum[2]), .C_out(full_adder_3_c_out));
  Full_Adder full_adder_4 (.A(B[3]), .B(A[3]), .C_in(full_adder_3_c_out), .S(Sum[3]), .C_out(C_out));
endmodule

module Program_Counter_SAP_1 (
  input  CLK,
  input  C_p,
  input  Enable,
  input  Clear,
  output [3:0] Out
);

  wire and_1_out, and_2_out, and_3_out;

  and and_1 (and_1_out, C_p, Out[0]);
  and and_2 (and_2_out, and_1_out, Out[1]);
  and and_3 (and_3_out, and_2_out, Out[2]);
  J_K_Flip_Flop j_k_ff_1 (.J(C_p), .clk(CLK), .K(C_p), .Q(Out[0]), .en(Enable), .reset(Clear));  // open: Qn, preset
  J_K_Flip_Flop j_k_ff_2 (
    .J(and_1_out), .clk(CLK), .K(and_1_out), .Q(Out[1]), .en(Enable), .reset(Clear));  // open: Qn, preset
  J_K_Flip_Flop j_k_ff_3 (
    .J(and_2_out), .clk(CLK), .K(and_2_out), .Q(Out[2]), .en(Enable), .reset(Clear));  // open: Qn, preset
  J_K_Flip_Flop j_k_ff_4 (
    .J(and_3_out), .clk(CLK), .K(and_3_out), .Q(Out[3]), .en(Enable), .reset(Clear));  // open: Qn, preset
endmodule

module ARM_PC (
  input  in_1,
  input  in_2,
  output [31:0] out_3
);

  wire clock_1_out;

  Clock clock_1 (.out(clock_1_out));
  Counter #(.width(30), .max('h3fffffff)) counter_1 (
    .Q(out_3[31:2]), .clk(clock_1_out));  // open: load, D, count, carry, clr

  assign out_3[1:0] = {in_2, in_1};
endmodule

module BITWISE_AND (
  input  [3:0] A,
  input  [3:0] B,
  output [3:0] C
);

  and and_1 (C[0], A[0], B[0]);
  and and_2 (C[1], A[1], B[1]);
  and and_3 (C[2], A[2], B[2]);
  and and_4 (C[3], A[3], B[3]);
endmodule

module BITWISE_XOR (
  input  [3:0] A,
  input  [3:0] B,
  output [3:0] C
);

  xor xor_1 (C[0], A[0], B[0]);
  xor xor_2 (C[1], A[1], B[1]);
  xor xor_3 (C[2], A[2], B[2]);
  xor xor_4 (C[3], A[3], B[3]);
endmodule

module BITWISE_NEGATION (
  input  [3:0] A,
  output [3:0] nA
);

  not not_1 (nA[0], A[0]);
  not not_2 (nA[2], A[2]);
  not not_3 (nA[1], A[1]);
  not not_4 (nA[3], A[3]);
endmodule

module MUX (
  input  [3:0] A,
  input  [3:0] B,
  input  in_3,
  input  [1:0] S,
  input  in_5,
  output [3:0] O
);

  wire [3:0] bitwise_and_1_c, bitwise_negation_1_na, bitwise_xor_1_c, multiplexer_1_out,
       ripple_carry_adder_1_sum;

  BITWISE_AND bitwise_and_1 (.A(A), .B(B), .C(bitwise_and_1_c));
  BITWISE_XOR bitwise_xor_1 (.A(A), .B(B), .C(bitwise_xor_1_c));
  BITWISE_NEGATION bitwise_negation_1 (.A(A), .nA(bitwise_negation_1_na));
  Ripple_Carry_Adder ripple_carry_adder_1 (.A(A), .B(B), .in_3(in_3), .Sum(ripple_carry_adder_1_sum));  // open: C_out
  Multiplexer #(.select(2), .width(4)) multiplexer_1 (
    .in0(bitwise_and_1_c), .in1(bitwise_xor_1_c), .in2(bitwise_negation_1_na),
    .in3(ripple_carry_adder_1_sum), .out(multiplexer_1_out), .sel(S));  // open: en
  assign O = in_5 ? multiplexer_1_out : 4'bz;  // Controlled_Buffer controlled_buffer_1

  // Notes on the sheet:
  //   AND
  //   XOR
  //   !A
  //   A+B
endmodule

module RING_COUNTER (
  output [3:0] out_1
);

  wire clock_1_out, xnor_1_out;

  Clock clock_1 (.out(clock_1_out));
  D_Flip_Flop d_ff_1 (.clk(clock_1_out), .D(xnor_1_out), .Q(out_1[0]));  // open: Qn, preset, en, reset
  D_Flip_Flop d_ff_2 (.clk(clock_1_out), .D(out_1[0]), .Q(out_1[1]));  // open: Qn, preset, en, reset
  NotExactlyOne xnor_1 (.out(xnor_1_out), .in1(out_1[3]), .in2(out_1[0]), .in3(out_1[1]), .in4(out_1[2]));
  D_Flip_Flop d_ff_3 (.clk(clock_1_out), .D(out_1[1]), .Q(out_1[2]));  // open: Qn, preset, en, reset
  D_Flip_Flop d_ff_4 (.clk(clock_1_out), .D(out_1[2]), .Q(out_1[3]));  // open: Qn, preset, en, reset
endmodule

module _2_s_adder (
  input  [3:0] A,
  input  [3:0] B,
  input  in_3,
  output [3:0] Sum,
  output C_out,
  output Overflow
);

  wire full_adder_1_c_out, full_adder_2_c_out, full_adder_3_c_out;
  wire [3:0] multiplexer_1_out, xor_1_out;

  Multiplexer #(.width(4), .enable("false")) multiplexer_1 (
    .in0(4'b0000), .in1(4'b1111), .out(multiplexer_1_out), .sel(in_3));
  assign xor_1_out = B ^ multiplexer_1_out;  // XOR_Gate xor_1, 4 bits wide
  Full_Adder full_adder_1 (.A(xor_1_out[0]), .B(A[0]), .C_in(in_3), .S(Sum[0]), .C_out(full_adder_1_c_out));
  Full_Adder full_adder_2 (
    .A(xor_1_out[1]), .B(A[1]), .C_in(full_adder_1_c_out), .S(Sum[1]), .C_out(full_adder_2_c_out));
  Full_Adder full_adder_3 (
    .A(xor_1_out[2]), .B(A[2]), .C_in(full_adder_2_c_out), .S(Sum[2]), .C_out(full_adder_3_c_out));
  Full_Adder full_adder_4 (.A(xor_1_out[3]), .B(A[3]), .C_in(full_adder_3_c_out), .S(Sum[3]), .C_out(C_out));
  xor xor_2 (Overflow, full_adder_3_c_out, C_out);
endmodule

module UMUX (
  input  in_1,
  input  [1:0] in_2,
  input  [1:0] in_3,
  input  [1:0] in_4,
  output out_5,
  output out_6,
  output out_7,
  output out_8
);

  Multiplexer #(.enable("false")) multiplexer_1 (.in0(1'b1), .in1(1'b0), .out(out_5), .sel(in_1));
  Multiplexer #(.select(2), .enable("false")) multiplexer_2 (
    .in0(1'b0), .in1(1'b1), .in2(1'b1), .in3(1'b1), .out(out_6), .sel(in_2));
  Multiplexer #(.select(2), .enable("false")) multiplexer_3 (
    .in0(1'b0), .in1(1'b0), .in2(1'b0), .in3(1'b1), .out(out_8), .sel(in_4));
  Multiplexer #(.select(2), .enable("false")) multiplexer_4 (
    .in0(1'b0), .in1(1'b1), .in2(1'b1), .in3(1'b0), .out(out_7), .sel(in_3));

  // Notes on the sheet:
  //   NOT
  //   OR
  //   AND
  //   XOR
endmodule

module REGFILE (
  input  [7:0] DATA,
  input  [2:0] ADDRESS,
  input  WE,
  input  [2:0] R1,
  input  [2:0] R2,
  input  RE,
  output [7:0] out_7,
  output [7:0] out_8
);

  wire clock_1_out, demultiplexer_2_out0, demultiplexer_2_out1, demultiplexer_2_out2, demultiplexer_2_out3,
       demultiplexer_2_out4, demultiplexer_2_out5, demultiplexer_2_out6, demultiplexer_2_out7;
  wire [7:0] demultiplexer_1_out0, demultiplexer_1_out1, demultiplexer_1_out2, demultiplexer_1_out3,
       demultiplexer_1_out4, demultiplexer_1_out5, demultiplexer_1_out6, demultiplexer_1_out7, register_1_q,
       register_2_q, register_3_q, register_4_q, register_5_q, register_6_q, register_7_q, register_8_q;

  Clock clock_1 (.out(clock_1_out));
  Demultiplexer #(.select(3), .width(8)) demultiplexer_1 (
    .out0(demultiplexer_1_out0), .out1(demultiplexer_1_out1), .out2(demultiplexer_1_out2),
    .out3(demultiplexer_1_out3), .out4(demultiplexer_1_out4), .out5(demultiplexer_1_out5),
    .out6(demultiplexer_1_out6), .out7(demultiplexer_1_out7), .in(DATA), .sel(ADDRESS), .en(WE));
  Demultiplexer #(.select(3), .enable("false")) demultiplexer_2 (
    .out0(demultiplexer_2_out0), .out1(demultiplexer_2_out1), .out2(demultiplexer_2_out2),
    .out3(demultiplexer_2_out3), .out4(demultiplexer_2_out4), .out5(demultiplexer_2_out5),
    .out6(demultiplexer_2_out6), .out7(demultiplexer_2_out7), .in(WE), .sel(ADDRESS));
  Register register_1 (
    .D(demultiplexer_1_out0), .en(demultiplexer_2_out0), .Q(register_1_q), .clk(clock_1_out));  // open: clr
  Register register_2 (
    .D(demultiplexer_1_out1), .en(demultiplexer_2_out1), .Q(register_2_q), .clk(clock_1_out));  // open: clr
  Register register_3 (
    .D(demultiplexer_1_out2), .en(demultiplexer_2_out2), .Q(register_3_q), .clk(clock_1_out));  // open: clr
  Register register_4 (
    .D(demultiplexer_1_out3), .en(demultiplexer_2_out3), .Q(register_4_q), .clk(clock_1_out));  // open: clr
  Register register_5 (
    .D(demultiplexer_1_out4), .en(demultiplexer_2_out4), .Q(register_5_q), .clk(clock_1_out));  // open: clr
  Register register_6 (
    .D(demultiplexer_1_out5), .en(demultiplexer_2_out5), .Q(register_6_q), .clk(clock_1_out));  // open: clr
  Register register_7 (
    .D(demultiplexer_1_out6), .en(demultiplexer_2_out6), .Q(register_7_q), .clk(clock_1_out));  // open: clr
  Register register_8 (
    .D(demultiplexer_1_out7), .en(demultiplexer_2_out7), .Q(register_8_q), .clk(clock_1_out));  // open: clr
  Multiplexer #(.select(3), .width(8)) multiplexer_1 (
    .in0(register_1_q), .in1(register_2_q), .in2(register_3_q), .in3(register_4_q), .in4(register_5_q),
    .in5(register_6_q), .in6(register_7_q), .in7(register_8_q), .out(out_7), .sel(R1), .en(RE));
  Multiplexer #(.select(3), .width(8)) multiplexer_2 (
    .in0(register_1_q), .in1(register_2_q), .in2(register_3_q), .in3(register_4_q), .in4(register_5_q),
    .in5(register_6_q), .in6(register_7_q), .in7(register_8_q), .out(out_8), .sel(R2), .en(RE));
endmodule
