// Logisim project sap1.circ as structural Verilog: 8 circuits, main circuit main
module main (
  output [3:0] ms,
  output [3:0] ls
);

  wire clock_1_out, controlled_buffer_1_out, controlled_buffer_2_out, controlled_buffer_3_out, CU_a_a,
       CU_acb, CU_b2o, CU_b2r, CU_br, CU_cp, CU_ea, CU_eab, CU_eir, CU_em, CU_ep, CU_hlt, CU_rb, not_1_out;
  wire [3:0] MAR_q, PC_q;
  wire [7:0] A_q, ALU_out_4, controlled_buffer_7_out, IR_q, multiplexer_1_out, OUT_q, Reg_B_q;

  assign controlled_buffer_1_out = not_1_out ? clock_1_out : 1'bz;  // Controlled_Buffer controlled_buffer_1
  Clock clock_1 (.out(clock_1_out));
  not not_1 (not_1_out, CU_hlt);
  assign controlled_buffer_2_out = CU_ep ? controlled_buffer_1_out : 1'bz;  // Controlled_Buffer controlled_buffer_2
  assign controlled_buffer_3_out = CU_br ? controlled_buffer_1_out : 1'bz;  // Controlled_Buffer controlled_buffer_3
  Counter #(.width(4), .max('hf)) PC (.Q(PC_q), .clk(controlled_buffer_2_out));  // open: load, D, count, carry, clr
  Register #(.width(4)) MAR (.D(ls), .en(CU_em), .Q(MAR_q), .clk(controlled_buffer_1_out));  // open: clr
  Register IR (.D({ms, ls}), .en(CU_eir), .Q(IR_q), .clk(controlled_buffer_1_out));  // open: clr
  assign ls = CU_cp ? PC_q : 4'bz;  // Controlled_Buffer controlled_buffer_4
  RAM_part #(.addrWidth(4)) ram_1 (
    .addr(MAR_q), .data({ms, ls}), .clk(controlled_buffer_3_out), .ld(CU_rb));  // open: sel, clr
  assign ls = CU_eab ? IR_q[3:0] : 4'bz;  // Controlled_Buffer controlled_buffer_5
  CU CU (
    .clock(controlled_buffer_1_out), .CP(CU_cp), .EP(CU_ep), .OP(IR_q[7:4]), .HLT(CU_hlt), .EM(CU_em),
    .RB(CU_rb), .BR(CU_br), .EIR(CU_eir), .EAB(CU_eab), .A_A(CU_a_a), .EA(CU_ea), .ACB(CU_acb), .B2R(CU_b2r),
    .B2O(CU_b2o));
  assign {ms, ls} = CU_acb ? A_q : 8'bz;  // Controlled_Buffer controlled_buffer_6
  Register A (.D(multiplexer_1_out), .en(CU_ea), .Q(A_q), .clk(controlled_buffer_1_out));  // open: clr
  Multiplexer #(.width(8), .enable("false")) multiplexer_1 (
    .in0({ms, ls}), .in1(controlled_buffer_7_out), .out(multiplexer_1_out), .sel(CU_a_a));
  ALU ALU (.AC(A_q), .B(Reg_B_q), .OP(IR_q[7:4]), .out_4(ALU_out_4));
  Register Reg_B (.D({ms, ls}), .en(CU_b2r), .Q(Reg_B_q), .clk(controlled_buffer_1_out));  // open: clr
  Register OUT (.D({ms, ls}), .en(CU_b2o), .Q(OUT_q), .clk(controlled_buffer_1_out));  // open: clr
  assign controlled_buffer_7_out = CU_a_a ? ALU_out_4 : 8'bz;  // Controlled_Buffer controlled_buffer_7
  Hex_Digit_Display hex_digit_display_1 (.value(OUT_q[7:4]));  // open: dp
  Hex_Digit_Display hex_digit_display_2 (.value(OUT_q[3:0]));  // open: dp

  // Notes on the sheet:
  //   PC
  //   RAM
  //   SAP
  //   Ajay Narayanan and S.Pawan Kumar.  
  //   IIITDM Kancheepuram.
  //   Operations supported
  //   HLT(Stop exection)
  //   LDA(load from an address at RAM onto AC)
  //   STA(store from AC onto an address at RAM
  //   NOT(Bitwise not of number in AC)
  //   OUT(Copy from AC to Out register)
  //   ADD(add number in AC with another number at an address in RAM)
  //   ORR(Bitwise or of the number in AC and at an address at RAM)
  //   SUB(substract number at an address in RAM from AC)
  //   AND(Bitwise and of the number in AC and at an address at RAM)
endmodule

module CU (
  input  clock,
  input  [3:0] OP,
  output CP,
  output EP,
  output HLT,
  output EM,
  output RB,
  output BR,
  output EIR,
  output EAB,
  output A_A,
  output EA,
  output ACB,
  output B2R,
  output B2O
);

  wire idec_1_add, idec_1_and, idec_1_lda, idec_1_not, idec_1_or, idec_1_out, idec_1_sta, idec_1_sub,
       nor_1_out, or_2_out, shift_register_1_q3, shift_register_1_q4, shift_register_1_q5;

  IDEC idec_1 (
    .OP(OP), .HLT(HLT), .LDA(idec_1_lda), .STA(idec_1_sta), .ADD(idec_1_add), .SUB(idec_1_sub),
    .OR(idec_1_or), .AND(idec_1_and), .NOT(idec_1_not), .OUT(idec_1_out));
  Shift_Register #(.length(6)) shift_register_1 (
    .in(nor_1_out), .clk(clock), .q0(CP), .q1(EP), .q2(EIR), .q3(shift_register_1_q3),
    .q4(shift_register_1_q4), .q5(shift_register_1_q5));  // open: shift, out, load, clr, d0, d1, d2, d3, d4, d5
  EM em_1 (
    .T1(CP), .T4(shift_register_1_q3), .LDR(idec_1_lda), .STA(idec_1_sta), .ADD(idec_1_add),
    .SUB(idec_1_sub), .AND(idec_1_and), .OR(idec_1_or), .EM(EM));
  RAM ram_1 (
    .T3(EIR), .T5(shift_register_1_q4), .AND(idec_1_and), .ADD(idec_1_add), .SUB(idec_1_sub),
    .LDA(idec_1_lda), .OR(idec_1_or), .STA(idec_1_sta), .RB(RB), .BR(BR));
  IR ir_1 (
    .T4(shift_register_1_q3), .AND(idec_1_and), .ADD(idec_1_add), .SUB(idec_1_sub), .LDA(idec_1_lda),
    .OR(idec_1_or), .STA(idec_1_sta), .EAB(EAB));
  or or_1 (A_A, idec_1_add, idec_1_sub, idec_1_and, idec_1_or, idec_1_not);
  AC ac_1 (
    .T4(shift_register_1_q3), .T5(shift_register_1_q4), .T6(shift_register_1_q5), .A_A(A_A),
    .LDA(idec_1_lda), .STA(idec_1_sta), .OUT(idec_1_out), .EA(EA), .ACB(ACB));
  or or_2 (or_2_out, idec_1_add, idec_1_sub, idec_1_or, idec_1_and);
  and and_1 (B2R, shift_register_1_q4, or_2_out);
  nor nor_1 (nor_1_out, CP, EP, EIR, shift_register_1_q3, shift_register_1_q4);
  and and_2 (B2O, shift_register_1_q3, idec_1_out);
endmodule

module IDEC (
  input  [3:0] OP,
  output HLT,
  output LDA,
  output STA,
  output ADD,
  output SUB,
  output OR,
  output AND,
  output NOT,
  output OUT
);

  Comparator #(.width(4), .mode("unsigned")) comparator_1 (.a(OP), .b(4'b1111), .eq(HLT));  // open: gt, lt
  Comparator #(.width(4), .mode("unsigned")) comparator_2 (.a(OP), .b(4'b0000), .eq(LDA));  // open: gt, lt
  Comparator #(.width(4), .mode("unsigned")) comparator_3 (.a(OP), .b(4'b0001), .eq(STA));  // open: gt, lt
  Comparator #(.width(4), .mode("unsigned")) comparator_4 (.a(OP), .b(4'b1011), .eq(ADD));  // open: gt, lt
  Comparator #(.width(4), .mode("unsigned")) comparator_5 (.a(OP), .b(4'b1100), .eq(SUB));  // open: gt, lt
  Comparator #(.width(4), .mode("unsigned")) comparator_6 (.a(OP), .b(4'b1010), .eq(OR));  // open: gt, lt
  Comparator #(.width(4), .mode("unsigned")) comparator_7 (.a(OP), .b(4'b1000), .eq(AND));  // open: gt, lt
  Comparator #(.width(4), .mode("unsigned")) comparator_8 (.a(OP), .b(4'b1001), .eq(NOT));  // open: gt, lt
  Comparator #(.width(4), .mode("unsigned")) comparator_9 (.a(OP), .b(4'b1101), .eq(OUT));  // open: gt, lt
endmodule

module EM (
  input  T1,
  input  T4,
  input  LDR,
  input  STA,
  input  ADD,
  input  SUB,
  input  AND,
  input  OR,
  output EM
);

  wire and_1_out, or_2_out;

  or or_1 (EM, T1, and_1_out);
  and and_1 (and_1_out, T4, or_2_out);
  or or_2 (or_2_out, LDR, STA, ADD, SUB, AND, OR);
endmodule

module ALU (
  input  [7:0] AC,
  input  [7:0] B,
  input  [3:0] OP,
  output [7:0] out_4
);

  wire [7:0] adder_1_out, adder_2_out, and_1_out, not_1_out, not_2_out, or_1_out;

  assign not_1_out = ~B;  // NOT_Gate not_1, 8 bits wide
  Adder adder_1 (.a(AC), .b(B), .out(adder_1_out));  // open: cin, cout
  Adder adder_2 (.a(AC), .b(not_1_out), .out(adder_2_out), .cin(1'b1));  // open: cout
  assign not_2_out = ~AC;  // NOT_Gate not_2, 8 bits wide
  assign or_1_out = AC | B;  // OR_Gate or_1, 8 bits wide
  assign and_1_out = AC & B;  // AND_Gate and_1, 8 bits wide
  Multiplexer #(.select(3), .width(8), .enable("false")) multiplexer_1 (
    .in0(and_1_out), .in1(not_2_out), .in2(or_1_out), .in3(adder_1_out), .in4(adder_2_out), .out(out_4),
    .sel(OP[2:0]));  // open: in5, in6, in7
endmodule

module RAM (
  input  T3,
  input  T5,
  input  AND,
  input  ADD,
  input  SUB,
  input  LDA,
  input  OR,
  input  STA,
  output RB,
  output BR
);

  wire and_1_out, or_2_out;

  or or_1 (RB, T3, and_1_out);
  or or_2 (or_2_out, AND, ADD, SUB, LDA, OR);
  and and_1 (and_1_out, T5, or_2_out);
  and and_2 (BR, T5, STA);
endmodule

module IR (
  input  T4,
  input  AND,
  input  ADD,
  input  SUB,
  input  LDA,
  input  OR,
  input  STA,
  output EAB
);

  wire or_1_out;

  or or_1 (or_1_out, AND, ADD, SUB, OR, STA, LDA);
  and and_1 (EAB, T4, or_1_out);
endmodule

module AC (
  input  T4,
  input  T5,
  input  T6,
  input  A_A,
  input  LDA,
  input  STA,
  input  OUT,
  output EA,
  output ACB
);

  wire and_1_out, and_2_out, and_3_out, and_4_out;

  and and_1 (and_1_out, T5, LDA);
  and and_2 (and_2_out, T6, A_A);
  or or_1 (EA, and_1_out, and_2_out);
  and and_3 (and_3_out, T5, STA);
  and and_4 (and_4_out, OUT, T4);
  or or_2 (ACB, and_3_out, and_4_out);
endmodule
